# Fritzing sketch well water alarm v3 (saved by Fritzing 0.9.3b)
breadboards: 1

parts:
  Part1 = Arduino Nano (Rev3.0)
  Adafruit_HUZZAH_ESP8266_Breakout1 = Adafruit HUZZAH ESP8266 Breakout [part_number=2471]
  Pressure_Sensor = Altitude/Pressure Sensor - MPL3115A2 Breakout [part_number=SEN-11084]
  U1 = LIPO-2000mAh [package=lipo-2000]
  Voltage_Reg_3_3V = Voltage Regulator LM1117 [package=sot223]
  Part2 = Power Cell LiPo Charger/Booster
  C1 = Capacitor Polarized [package=panasonic_d]

nets:
  GND: Part1.GND, Pressure_Sensor.GND
  N1: Part1.D2, Adafruit_HUZZAH_ESP8266_Breakout1.TX
  N2: Part1.D3, Adafruit_HUZZAH_ESP8266_Breakout1.RX
  5V: Part1.5V, Pressure_Sensor.VCC
  N3: Part1.A0, Pressure_Sensor.SCL
  N4: Adafruit_HUZZAH_ESP8266_Breakout1.#12, Adafruit_HUZZAH_ESP8266_Breakout1.V+, U1.-, Voltage_Reg_3_3V.OUT, Part2.GND, C1.-
  N5: Adafruit_HUZZAH_ESP8266_Breakout1.GND, Voltage_Reg_3_3V.IN, C1.+
  N6: U1.+, Part2.5VIN
  N7: Voltage_Reg_3_3V.ADJ, Part2.VCC

custom parts:
  Arduino Nano (Rev3.0): The Arduino Nano is a small, complete, and breadboard-friendly board based on the ATmega328 (Arduino Nano 3.0) or ATmega168 (Arduino Nano 2.x). It has more or less the same functionality of the Arduino Duemilanove, but in a different package. It lacks only a DC power jack, and works with a Mini-B USB cable instead of a standard one. The Nano was designed and is being produced by Gravitech.
